# Fritzing sketch Stm32-VFO (saved by Fritzing 0.9.3b)
breadboards: 1

parts:
  U1 = BluePill
  U2 = ST7735 1.8 inch TFT LCD [package="SIP (Single Inline) [THT]"]
  IC1 = 24LC16 [package=THT]
  Part1 = Adafruit Si5351A Clock Generator [part_number="Adafruit #2045"]

nets:
  N1: U1.B10, IC1.SCL_-_I2C_Clock, Part1.SCL
  N2: U1.B11, IC1.SDA_-_I2C_Data, Part1.SDA
  3V3: U1.3V3, U2.VCC, U2.LED, IC1.+V, Part1.VIN
  GND: U1.GND, U2.GND, IC1.0V, Part1.GND
  N3: U1.A12, U2.CS
  N4: U1.A10, U2.RST
  N5: U1.A9, U2.A0
  N6: U1.B15, U2.SDA
  N7: U1.B13, U2.SCK

custom parts:
  ST7735 1.8 inch TFT LCD: 1.8 inch TFT LCD module. SPI interface, ST7735 controller
  Adafruit Si5351A Clock Generator: Never hunt around for another crystal again, with the Si5351A clock generator breakout from Adafruit! This chip has a precision 25MHz crystal reference and internal PLL and dividers so it can generate just about any frequency, from <8KHz up to 150+ MHz. The Si5351A clock generator is an I2C controller clock generator. It uses the onboard precision clock to drive multiple PLL's and clock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
